// Logisim project ex4.circ as structural Verilog: 1 circuit, main circuit Split
module Split (
  input  [7:0] In1,
  output Out1,
  output [7:0] Out2
);

  not not_1 (Out2[7], In1[7]);
  and and_1 (Out1, In1[0], In1[7]);

  assign Out2[6:0] = In1[6:0];

  // Notes on the sheet:
  //   PUT CIRCUITRY HERE
  //   Question 8 answer, the output1 will be 1 if the two's comp. number is negative (MSB is 1) and odd (LSB is 1)
endmodule
