// Logisim project cpu.circ as structural Verilog: 1 circuit, main circuit cpu
module cpu (
  input  clk,
  input  [31:0] INSTRUCTION,
  input  [31:0] READ_DATA,
  output [31:0] WRITE_ADDRESS,
  output [31:0] PROGRAM_COUNTER,
  output [31:0] ra,
  output [31:0] sp,
  output [31:0] t0,
  output [31:0] t1,
  output [31:0] t2,
  output [31:0] s0,
  output [31:0] s1,
  output [31:0] a0,
  output [31:0] tohost,
  output [3:0] WRITE_ENABLE,
  output [31:0] WRITE_DATA
);

  wire RegWEn;
  wire [1:0] WBSel;
  wire [2:0] immSel;
  wire [3:0] ALUsel;
  wire [31:0] adder_1_out, alu_1_result, aluMA, DataA, imm, InstEX, InstID, InstMA, InstWB, PCID;

  Register #(.width(32)) register_1 (.D(InstID), .clk(clk), .Q(InstEX));  // open: en, clr
  Adder #(.width(32)) adder_1 (.a(PROGRAM_COUNTER), .b(32'h4), .out(adder_1_out));  // open: cin, cout
  Register #(.width(32)) PC (.D(adder_1_out), .clk(clk), .Q(PROGRAM_COUNTER));  // open: en, clr
  Register #(.width(32)) register_2 (.D(PROGRAM_COUNTER), .clk(clk), .Q(PCID));  // open: en, clr
  Register #(.width(32)) register_3 (.D(INSTRUCTION), .clk(clk), .Q(InstID));  // open: en, clr
  // control_logic control_logic_1: pin names not known; wires that end beside it: RegWEn, immSel
  imm_gen imm_gen_1 (.inst(InstEX), .ImmSel(immSel), .imm(imm));
  Register #(.width(32)) register_4 (.D(InstEX), .clk(clk), .Q(InstMA));  // open: en, clr
  Register #(.width(32)) register_5 (.D(InstMA), .clk(clk), .Q(InstWB));  // open: en, clr
  // branch_comp branch_comp_1: pin names not known; wires that end beside it: ALUsel, WBSel
  regfile regfile_1 (
    .rs1(InstID[19:15]), .rs2(InstID[24:20]), .rd(InstWB[11:7]), .Write_Data(aluMA), .RegWEn(1'b1),
    .clk(clk), .ra(ra), .sp(sp), .t0(t0), .t1(t1), .t2(t2), .s0(s0), .s1(s1), .a0(a0), .Read_Data_1(DataA),
    .Read_Data_2(WRITE_DATA));
  // csr csr_1: pin names not known; wires that end beside it: tohost
  Register #(.width(32)) register_6 (.D(alu_1_result), .clk(clk), .Q(aluMA));  // open: en, clr
  alu alu_1 (.Result(alu_1_result), .A(DataA), .B(imm), .ALUSel(ALUsel));
  Multiplexer #(.enable("false"), .select(2), .width(32)) multiplexer_1 (
    .in0(WRITE_ADDRESS), .in1(READ_DATA), .sel(WBSel));  // open: in2, in3, out

  // Other names for the same wires on the sheet: DataB[31:0] = WRITE_DATA

  // Notes on the sheet:
  //   Output to IMEM
  //   IMEM (do **NOT** move this)
  //   Inputs from IMEM
  //   Inputs/Outputs for testing. Do **NOT** move these.
  //   Outputs To DMEM
  //   DMEM (do **NOT** move this)
  //   Inputs From DMEM
endmodule
